# Fritzing sketch ADC (saved by Fritzing 0.9.3b)
circuit board: 8.46667cm x 5.64444cm
breadboards: 1

parts:
  Part1 = Arduino Uno (Rev3)
  VR1 = Rotary Potentiometer (Small) [maximum_resistance=100kΩ package=THT]
  LED1 = LED - 5mm [color="Red (633nm)" package="5 mm [THT]"]
  R1 = Resistor [tolerance=±5% resistance=560 package=THT]

nets:
  N1: Part1.A0, VR1.wiper
  N2: Part1.D9_PWM, R1.Pin_0
  N3: Part1.GND, VR1.leg1, LED1.cathode
  N4: Part1.5V, VR1.leg2
  N5: LED1.anode, R1.Pin_1

notes:
  GND
  D9
  5V
  A0
