# Fritzing sketch Comparator (saved by Fritzing 0.9.3b)
breadboards: 1

parts:
  R1 = Resistor [tolerance=±5% resistance=560 package=THT]
  R2 = Resistor [tolerance=±5% resistance=560 package=THT]
  Part1 = Arduino Uno (Rev3)
  VR1 = Rotary Potentiometer (Small) [maximum_resistance=10kΩ package=THT]
  R3 = Resistor [tolerance=±5% resistance=560 package=THT]
  LED1 = LED - 5mm [color="Red (633nm)" package="5 mm [THT]"]

nets:
  VCC: R1.Pin_0, Part1.5V, VR1.leg1
  N1: R1.Pin_1, R2.Pin_0, Part1.D6_PWM
  GND: R2.Pin_1, Part1.GND, VR1.leg2, LED1.cathode
  N2: Part1.D13/SCK, R3.Pin_1
  AIN1/D7: Part1.D7, VR1.wiper
  N3: R3.Pin_0, LED1.anode
